// Logisim project Projeto Comparador.circ as structural Verilog: 1 circuit, main circuit main
module main (
  input  A3,
  input  B3,
  input  A2,
  input  B2,
  input  A1,
  input  B1,
  input  A0,
  input  B1_2
);

  wire A0_B0_out, A1_B1_out, A2_B2_out, A3_B3_2_out, A3_B3_AND_A2_B2_AND_A1_B1_AND_A0_B0_out,
       A3_B3_AND_A2_B2_AND_A1_B1_out, A3_B3_AND_A2_B2_out, A3_B3_out, A_B_2_out, A_B_3_out, A_B_OR_A_B_out,
       A_B_out, not_1_out, not_2_out, not_3_out, not_4_out;

  not not_1 (not_1_out, B3);
  not not_2 (not_2_out, B2);
  not not_3 (not_3_out, B1);
  not not_4 (not_4_out, B1_2);
  and A3_B3 (A3_B3_out, A3, not_1_out);
  xnor A3_B3_2 (A3_B3_2_out, A3, B3);
  xnor A2_B2 (A2_B2_out, A2, B2);
  xnor A1_B1 (A1_B1_out, A1, B1);
  xnor A0_B0 (A0_B0_out, A0, B1_2);
  and A3_B3_AND_A2_B2_AND_A1_B1 (A3_B3_AND_A2_B2_AND_A1_B1_out, A3_B3_2_out, A2_B2_out, A1, not_3_out);
  and A3_B3_AND_A2_B2_AND_A1_B1_AND_A0_B0 (A3_B3_AND_A2_B2_AND_A1_B1_AND_A0_B0_out, A3_B3_2_out, A2_B2_out, A1_B1_out, A0, not_4_out);
  and A3_B3_AND_A2_B2 (A3_B3_AND_A2_B2_out, A3_B3_2_out, A2, not_2_out);
  and A_B (A_B_out, A3_B3_2_out, A2_B2_out, A1_B1_out, A0_B0_out);
  or A_B_2 (A_B_2_out, A3_B3_out, A3_B3_AND_A2_B2_out, A3_B3_AND_A2_B2_AND_A1_B1_out, A3_B3_AND_A2_B2_AND_A1_B1_AND_A0_B0_out);
  LED Y6 (.in(1'b0));
  LED Y7 (.in(1'b1));
  nor A_B_3 (A_B_3_out, A_B_2_out, A_B_out);
  LED Y5 (.in(1'b1));
  LED Y4 (.in(A_B_3_out));
  LED Y3 (.in(1'b1));
  or A_B_OR_A_B (A_B_OR_A_B_out, A_B_out, A_B_3_out);
  LED Y1 (.in(1'b1));
  LED Y2 (.in(1'b0));
  LED Y0 (.in(A_B_OR_A_B_out));
endmodule
