// Logisim project Comparador.circ as structural Verilog: 1 circuit, main circuit main
module main (
  input  A3,
  input  B3,
  input  A2,
  input  B2,
  input  A1,
  input  B1,
  input  A0,
  input  B0,
  output Y7,
  output Y6,
  output Y5,
  output Y4,
  output Y3,
  output Y2,
  output Y1,
  output Y0
);

  wire A0_B0_2_out, A0_B0_out, A1_B1_2_out, A1_B1_out, A2_B2_2_out, A2_B2_out, A3_B3_2_out, A3_B3_out,
       A_B_2_out, E_2_out, E_3_out, E_out;

  and A3_B3 (A3_B3_out, ~A3, B3);  // AND_Gate
  xnor A3_B3_2 (A3_B3_2_out, A3, B3);
  and A2_B2 (A2_B2_out, ~A2, B2);  // AND_Gate
  xnor A2_B2_2 (A2_B2_2_out, A2, B2);
  and A1_B1 (A1_B1_out, ~A1, B1);  // AND_Gate
  xnor A1_B1_2 (A1_B1_2_out, A1, B1);
  and A0_B0 (A0_B0_out, ~A0, B0);  // AND_Gate
  xnor A0_B0_2 (A0_B0_2_out, A0, B0);
  and E (E_out, A3_B3_2_out, A2_B2_2_out, A1_B1_out);
  and E_2 (E_2_out, A3_B3_2_out, A2_B2_out);
  and E_3 (E_3_out, A3_B3_2_out, A2_B2_2_out, A1_B1_2_out, A0_B0_out);
  or A_B (Y4, A3_B3_out, E_2_out, E_out, E_3_out);
  and A_B_2 (A_B_2_out, A3_B3_2_out, A2_B2_2_out, A1_B1_2_out, A0_B0_2_out);
  // AND_Gate A_B_3 has open pins: in0=Y4, in4=A_B_2_out, out=open
  or A_B_ou_A_B (Y0, Y4, A_B_2_out);

  assign Y1 = 1'b1;
  assign Y2 = 1'b0;
  assign Y3 = 1'b1;
  assign Y5 = 1'b1;
  assign Y6 = 1'b0;
  assign Y7 = 1'b1;
endmodule
