// Logisim project Conversor.circ as structural Verilog: 1 circuit, main circuit main
module main (
  input  B3,
  input  B2,
  input  in_3,
  input  B1,
  input  B0,
  output X3,
  output X2,
  output X1,
  output X0
);

  wire multiplexer_1_out, multiplexer_2_out;

  Multiplexer #(.enable("false")) multiplexer_1 (.in0(B2), .in1(X2), .out(multiplexer_1_out), .sel(in_3));
  Multiplexer #(.enable("false")) multiplexer_2 (.in0(B1), .in1(X1), .out(multiplexer_2_out), .sel(in_3));
  xor xor_1 (X2, B3, B2);
  xor xor_2 (X1, multiplexer_1_out, B1);
  xor xor_3 (X0, multiplexer_2_out, B0);

  assign X3 = B3;
endmodule
