// Logisim project Display.circ as structural Verilog: 2 circuits, main circuit main
// MAIN
module main (
  input  A,
  input  B,
  input  C,
  input  D,
  output A_2,
  output B_2,
  output C_2,
  output D_2,
  output E,
  output F,
  output G
);

  wire A_prime_B_out, A_prime_BC_prime_2_out, A_prime_BC_prime_D_out, A_prime_BC_prime_out, A_prime_BD_out,
       A_prime_BD_prime_2_out, A_prime_BD_prime_out, A_prime_C_out, A_prime_C_prime_D_prime_out,
       A_prime_C_prime_out, A_prime_CD_out, A_prime_CD_prime_2_out, A_prime_CD_prime_out, A_prime_D_out,
       AB_prime_2_out, AB_prime_3_out, AB_prime_C_out, AB_prime_C_prime_out, AB_prime_D_out, AB_prime_out,
       AC_prime_D_prime_2_out, AC_prime_D_prime_3_out, AC_prime_D_prime_out, B_prime_C_out,
       B_prime_C_prime_D_prime_out, B_prime_C_prime_out, B_prime_CD_out, B_prime_D_prime_2_out,
       B_prime_D_prime_3_out, B_prime_D_prime_out, C_prime_D_prime_out, not_1_out, not_2_out, not_3_out,
       not_4_out;

  not not_1 (not_1_out, A);
  not not_2 (not_2_out, B);
  not not_3 (not_3_out, C);
  not not_4 (not_4_out, D);
  and A_prime_C (A_prime_C_out, not_1_out, C);
  and A_prime_BD (A_prime_BD_out, not_1_out, B, D);
  and B_prime_D_prime (B_prime_D_prime_out, not_2_out, not_4_out);
  or or_1 (A_2, A_prime_C_out, B_prime_D_prime_out, A_prime_BD_out, AC_prime_D_prime_out, AB_prime_C_prime_out);
  and AC_prime_D_prime (AC_prime_D_prime_out, A, not_3_out, not_4_out);
  and AB_prime_C_prime (AB_prime_C_prime_out, A, not_2_out, not_3_out);
  and B_prime_C_prime (B_prime_C_prime_out, not_2_out, not_3_out);
  and B_prime_D_prime_2 (B_prime_D_prime_2_out, not_2_out, not_4_out);
  and A_prime_C_prime_D_prime (A_prime_C_prime_D_prime_out, not_1_out, not_3_out, not_4_out);
  or or_2 (B_2, B_prime_C_prime_out, B_prime_D_prime_2_out, A_prime_C_prime_D_prime_out, A_prime_CD_out);
  and A_prime_CD (A_prime_CD_out, not_1_out, C, D);
  and A_prime_B (A_prime_B_out, not_1_out, B);
  and AB_prime (AB_prime_out, A, not_2_out);
  and A_prime_C_prime (A_prime_C_prime_out, not_1_out, not_3_out);
  or or_3 (C_2, A_prime_B_out, AB_prime_out, A_prime_C_prime_out, A_prime_D_out);
  and A_prime_D (A_prime_D_out, not_1_out, D);
  and A_prime_CD_prime (A_prime_CD_prime_out, not_1_out, C, not_4_out);
  and B_prime_CD (B_prime_CD_out, not_2_out, C, D);
  and AC_prime_D_prime_2 (AC_prime_D_prime_2_out, A, not_3_out, not_4_out);
  or or_4 (D_2, A_prime_CD_prime_out, B_prime_CD_out, AC_prime_D_prime_2_out, B_prime_C_prime_D_prime_out, AB_prime_D_out, A_prime_BC_prime_D_out);
  and B_prime_C_prime_D_prime (B_prime_C_prime_D_prime_out, not_2_out, not_3_out, not_4_out);
  and A_prime_BC_prime_D (A_prime_BC_prime_D_out, not_1_out, B, not_3_out, D);
  and AB_prime_D (AB_prime_D_out, A, not_2_out, D);
  and A_prime_CD_prime_2 (A_prime_CD_prime_2_out, not_1_out, C, not_4_out);
  and B_prime_D_prime_3 (B_prime_D_prime_3_out, not_2_out, not_4_out);
  and AC_prime_D_prime_3 (AC_prime_D_prime_3_out, A, not_3_out, not_4_out);
  or or_5 (E, B_prime_D_prime_3_out, A_prime_CD_prime_2_out, AC_prime_D_prime_3_out, AB_prime_C_out);
  and AB_prime_C (AB_prime_C_out, A, not_2_out, C);
  and AB_prime_2 (AB_prime_2_out, A, not_2_out);
  and C_prime_D_prime (C_prime_D_prime_out, not_3_out, not_4_out);
  and A_prime_BC_prime (A_prime_BC_prime_out, not_1_out, B, not_3_out);
  or or_6 (F, AB_prime_2_out, C_prime_D_prime_out, A_prime_BC_prime_out, A_prime_BD_prime_out);
  and A_prime_BD_prime (A_prime_BD_prime_out, not_1_out, B, not_4_out);
  and AB_prime_3 (AB_prime_3_out, A, not_2_out);
  and B_prime_C (B_prime_C_out, not_2_out, C);
  or or_7 (G, AB_prime_3_out, B_prime_C_out, A_prime_BC_prime_2_out, A_prime_BD_prime_2_out);
  and A_prime_BC_prime_2 (A_prime_BC_prime_2_out, not_1_out, B, not_3_out);
  and A_prime_BD_prime_2 (A_prime_BD_prime_2_out, not_1_out, B, not_4_out);

  // Notes on the sheet:
  //   A'
  //   B'
  //   C'
  //   D'
  //   A'C + B'D' + A'BD + AC'D' + AB'C'
  //   B'C' + B'D' + A'C'D' + A'CD
  //   A'B + AB' + A'C' + A'D
  //   A'CD' + B'CD + AC'D' + B'C'D' + AB'D + A'BC'D
  //   B'D' + A'CD' + AC'D'  + AB'C
  //   AB' + C'D' + A'BC' + A'BD'
  //   AB' + B'C + A'BC' + A'BD'
endmodule

module Mux_Dmux (
  input  [3:0] X,
  input  [3:0] Y,
  input  SEL
);

  wire AX, AY, BX, BY, CX, CY, DX, DY, EX, EY, FX, FY, GX, GY;
  wire [3:0] multiplexer_1_out;
  wire [6:0] main_1_g;

  Multiplexer #(.width(4), .enable("false")) multiplexer_1 (.in0(X), .in1(Y), .out(multiplexer_1_out), .sel(SEL));
  main main_1 (
    .A(multiplexer_1_out[3]), .B(multiplexer_1_out[2]), .C(multiplexer_1_out[1]), .D(multiplexer_1_out[0]),
    .B_2(main_1_g[5]), .C_2(main_1_g[4]), .D_2(main_1_g[3]), .E(main_1_g[2]), .F(main_1_g[1]),
    .G(main_1_g[0]), .A_2(main_1_g[6]));
  _7_Segment_Display u_7_segment_display_1 (.g(GX), .f(FX), .a(AX), .b(BX), .e(EX), .d(DX), .c(CX));  // open: dp
  Demultiplexer #(.width(7), .enable("false")) demultiplexer_1 (
    .out0({AX, BX, CX, DX, EX, FX, GX}), .out1({AY, BY, CY, DY, EY, FY, GY}), .in(main_1_g), .sel(SEL));
  _7_Segment_Display u_7_segment_display_2 (.g(GY), .f(FY), .a(AY), .b(BY), .e(EY), .d(DY), .c(CY));  // open: dp

  // Notes on the sheet:
  //   8 4 2 1
endmodule
