// Logisim project Trabalho GA.circ as structural Verilog
// CY
module main (
  input  START,
  input  RESET,
  input  [3:0] A,
  input  [3:0] B,
  output [1:0] OUT
);

  wire A__B, and_1_out, and_2_out, and_3_out, and_4_out, and_5_out, and_6_out, C, CLK_out, display_1_ax,
       display_1_bx, display_1_cx, display_1_dx, display_1_ex, display_1_fx, display_1_gx, display_2_ax,
       display_2_bx, display_2_cx, display_2_dx, display_2_ex, display_2_fx, display_2_gx, E0, E1, P0, P1;
  wire [2:0] multiplexer_1_out;
  wire [7:0] A_B_out_3, A_e_B_Gray_out_3, multiplexer_2_out;

  and and_1 (and_1_out, E1, ~E0);  // AND_Gate
  or or_1 (P1, and_1_out, and_2_out, and_3_out);
  and and_2 (and_2_out, E1, ~C);  // AND_Gate
  and and_3 (and_3_out, ~E1, E0, C);  // AND_Gate
  and and_4 (and_4_out, E0, ~C);  // AND_Gate
  or or_2 (P0, and_4_out, and_5_out, and_6_out);
  and and_5 (and_5_out, ~E1, ~E0, START);  // AND_Gate
  and and_6 (and_6_out, ~E1, E0, ~A__B);  // AND_Gate
  and and_7 (OUT[1], E1, E0);
  and and_8 (OUT[0], ~E1, E0);  // AND_Gate
  Clock CLK (.out(CLK_out));
  Register #(.width(1)) u_E1 (.D(P1), .Q(E1), .clk(CLK_out), .clr(RESET));  // open: en
  Register #(.width(1)) u_E0 (.D(P0), .Q(E0), .clk(CLK_out), .clr(RESET));  // open: en
  Multiplexer #(.select(2), .width(3), .enable("false")) multiplexer_1 (
    .in0(3'b000), .in1(3'b101), .in2(3'b111), .out(multiplexer_1_out), .sel(OUT));  // open: in3
  Counter #(.width(3), .max('h7), .ongoal("load"), .trigger("falling")) Contador (
    .load(1'b1), .D(multiplexer_1_out), .count(1'b1), .carry(C), .clk(CLK_out), .clr(RESET));  // open: Q
  Comparador u_A__B (.A(A), .B(B), .out_3(A__B));
  Subtrator A_B (.A(A), .B(B), .out_3(A_B_out_3));
  Conversor_Gray A_e_B_Gray (.A(A), .B(B), .out_3(A_e_B_Gray_out_3));
  Multiplexer #(.select(2), .width(8), .enable("false")) multiplexer_2 (
    .in0({8{1'b1}}), .in1({B, A}), .in2(A_B_out_3), .in3(A_e_B_Gray_out_3), .out(multiplexer_2_out),
    .sel({E1, E0}));
  Display display_1 (
    .X(multiplexer_2_out[3:0]), .Ax(display_1_ax), .Bx(display_1_bx), .Cx(display_1_cx), .Dx(display_1_dx),
    .Ex(display_1_ex), .Fx(display_1_fx), .Gx(display_1_gx));
  Display display_2 (
    .X(multiplexer_2_out[7:4]), .Ax(display_2_ax), .Bx(display_2_bx), .Cx(display_2_cx), .Dx(display_2_dx),
    .Ex(display_2_ex), .Fx(display_2_fx), .Gx(display_2_gx));
  _7_Segment_Display u_7_segment_display_1 (
    .g(display_1_gx), .f(display_1_fx), .a(display_1_ax), .b(display_1_bx), .e(display_1_ex),
    .d(display_1_dx), .c(display_1_cx));  // open: dp
  _7_Segment_Display u_7_segment_display_2 (
    .g(display_2_gx), .f(display_2_fx), .a(display_2_ax), .b(display_2_bx), .e(display_2_ex),
    .d(display_2_dx), .c(display_2_cx));  // open: dp

  // Other names for the same wires on the sheet: MUX[1:0] = OUT; R = RESET; S1_S0[1:0] = {E1, E0}

  // Notes on the sheet:
  //   8 4 2 1
  //   8 4 2 1
endmodule

module Display_Auxiliar (
  input  A,
  input  B,
  input  C,
  input  D,
  output A_2,
  output B_2,
  output C_2,
  output D_2,
  output E,
  output F,
  output G
);

  wire A_prime_B_out, A_prime_BC_prime_2_out, A_prime_BC_prime_D_out, A_prime_BC_prime_out, A_prime_BD_out,
       A_prime_BD_prime_2_out, A_prime_BD_prime_out, A_prime_C_out, A_prime_C_prime_D_prime_out,
       A_prime_C_prime_out, A_prime_CD_out, A_prime_CD_prime_2_out, A_prime_CD_prime_out, A_prime_D_out,
       AB_prime_2_out, AB_prime_3_out, AB_prime_C_out, AB_prime_C_prime_out, AB_prime_D_out, AB_prime_out,
       AC_prime_D_prime_2_out, AC_prime_D_prime_3_out, AC_prime_D_prime_out, B_prime_C_out,
       B_prime_C_prime_D_prime_out, B_prime_C_prime_out, B_prime_CD_out, B_prime_D_prime_2_out,
       B_prime_D_prime_3_out, B_prime_D_prime_out, C_prime_D_prime_out, not_1_out, not_2_out, not_3_out,
       not_4_out;

  not not_1 (not_1_out, A);
  not not_2 (not_2_out, B);
  not not_3 (not_3_out, C);
  not not_4 (not_4_out, D);
  and A_prime_C (A_prime_C_out, not_1_out, C);
  and B_prime_D_prime (B_prime_D_prime_out, not_2_out, not_4_out);
  and A_prime_BD (A_prime_BD_out, not_1_out, B, D);
  or or_1 (A_2, A_prime_C_out, B_prime_D_prime_out, A_prime_BD_out, AC_prime_D_prime_out, AB_prime_C_prime_out);
  and AC_prime_D_prime (AC_prime_D_prime_out, A, not_3_out, not_4_out);
  and AB_prime_C_prime (AB_prime_C_prime_out, A, not_2_out, not_3_out);
  and B_prime_C_prime (B_prime_C_prime_out, not_2_out, not_3_out);
  and B_prime_D_prime_2 (B_prime_D_prime_2_out, not_2_out, not_4_out);
  and A_prime_C_prime_D_prime (A_prime_C_prime_D_prime_out, not_1_out, not_3_out, not_4_out);
  or or_2 (B_2, B_prime_C_prime_out, B_prime_D_prime_2_out, A_prime_C_prime_D_prime_out, A_prime_CD_out);
  and A_prime_CD (A_prime_CD_out, not_1_out, C, D);
  and A_prime_B (A_prime_B_out, not_1_out, B);
  and AB_prime (AB_prime_out, A, not_2_out);
  and A_prime_C_prime (A_prime_C_prime_out, not_1_out, not_3_out);
  or or_3 (C_2, A_prime_B_out, AB_prime_out, A_prime_C_prime_out, A_prime_D_out);
  and A_prime_D (A_prime_D_out, not_1_out, D);
  and A_prime_CD_prime (A_prime_CD_prime_out, not_1_out, C, not_4_out);
  and B_prime_CD (B_prime_CD_out, not_2_out, C, D);
  and AC_prime_D_prime_2 (AC_prime_D_prime_2_out, A, not_3_out, not_4_out);
  or or_4 (D_2, A_prime_CD_prime_out, B_prime_CD_out, AC_prime_D_prime_2_out, B_prime_C_prime_D_prime_out, AB_prime_D_out, A_prime_BC_prime_D_out);
  and B_prime_C_prime_D_prime (B_prime_C_prime_D_prime_out, not_2_out, not_3_out, not_4_out);
  and AB_prime_D (AB_prime_D_out, A, not_2_out, D);
  and A_prime_BC_prime_D (A_prime_BC_prime_D_out, not_1_out, B, not_3_out, D);
  and B_prime_D_prime_3 (B_prime_D_prime_3_out, not_2_out, not_4_out);
  and A_prime_CD_prime_2 (A_prime_CD_prime_2_out, not_1_out, C, not_4_out);
  and AC_prime_D_prime_3 (AC_prime_D_prime_3_out, A, not_3_out, not_4_out);
  or or_5 (E, B_prime_D_prime_3_out, A_prime_CD_prime_2_out, AC_prime_D_prime_3_out, AB_prime_C_out);
  and AB_prime_C (AB_prime_C_out, A, not_2_out, C);
  and AB_prime_2 (AB_prime_2_out, A, not_2_out);
  and C_prime_D_prime (C_prime_D_prime_out, not_3_out, not_4_out);
  and A_prime_BC_prime (A_prime_BC_prime_out, not_1_out, B, not_3_out);
  or or_6 (F, AB_prime_2_out, C_prime_D_prime_out, A_prime_BC_prime_out, A_prime_BD_prime_out);
  and A_prime_BD_prime (A_prime_BD_prime_out, not_1_out, B, not_4_out);
  and AB_prime_3 (AB_prime_3_out, A, not_2_out);
  and B_prime_C (B_prime_C_out, not_2_out, C);
  or or_7 (G, AB_prime_3_out, B_prime_C_out, A_prime_BC_prime_2_out, A_prime_BD_prime_2_out);
  and A_prime_BC_prime_2 (A_prime_BC_prime_2_out, not_1_out, B, not_3_out);
  and A_prime_BD_prime_2 (A_prime_BD_prime_2_out, not_1_out, B, not_4_out);

  // Notes on the sheet:
  //   A'
  //   B'
  //   C'
  //   D'
  //   A'C + B'D' + A'BD + AC'D' + AB'C'
  //   B'C' + B'D' + A'C'D' + A'CD
  //   A'B + AB' + A'C' + A'D
  //   A'CD' + B'CD + AC'D' + B'C'D' + AB'D + A'BC'D
  //   B'D' + A'CD' + AC'D'  + AB'C
  //   AB' + C'D' + A'BC' + A'BD'
  //   AB' + B'C + A'BC' + A'BD'
endmodule

module Display (
  input  [3:0] X,
  output Ax,
  output Bx,
  output Cx,
  output Dx,
  output Ex,
  output Fx,
  output Gx
);

  Display_main main_1 (
    .A(X[3]), .B(X[2]), .C(X[1]), .D(X[0]), .B_2(Bx), .C_2(Cx), .D_2(Dx), .E(Ex), .F(Fx), .G(Gx), .A_2(Ax));

  // Notes on the sheet:
  //   8 4 2 1
endmodule

module Subtrator (
  input  [3:0] A,
  input  [3:0] B,
  output [7:0] out_3
);

  wire and_1_out, and_2_out, and_3_out, and_4_out, and_5_out, and_6_out, and_7_out, and_8_out, not_1_out,
       or_1_out, or_2_out, or_3_out, or_4_out, xor_1_out, xor_2_out, xor_3_out, xor_4_out, xor_5_out,
       xor_6_out, xor_7_out, xor_8_out;

  not not_1 (not_1_out, 1'b0);
  xor xor_1 (xor_1_out, not_1_out, B[0]);
  xor xor_2 (xor_2_out, not_1_out, B[1]);
  xor xor_3 (xor_3_out, not_1_out, B[2]);
  xor xor_4 (xor_4_out, not_1_out, B[3]);
  xor xor_5 (xor_5_out, A[0], xor_1_out);
  and and_1 (and_1_out, A[0], xor_1_out);
  xor xor_6 (xor_6_out, A[1], xor_2_out);
  and and_2 (and_2_out, A[1], xor_2_out);
  xor xor_7 (xor_7_out, A[2], xor_3_out);
  and and_3 (and_3_out, A[2], xor_3_out);
  xor xor_8 (xor_8_out, A[3], xor_4_out);
  and and_4 (and_4_out, A[3], xor_4_out);
  xor xor_9 (out_3[4], xor_5_out, not_1_out);
  and and_5 (and_5_out, not_1_out, xor_5_out);
  xor xor_10 (out_3[5], xor_6_out, or_1_out);
  and and_6 (and_6_out, or_1_out, xor_6_out);
  xor xor_11 (out_3[6], xor_7_out, or_2_out);
  and and_7 (and_7_out, or_2_out, xor_7_out);
  xor xor_12 (out_3[7], xor_8_out, or_3_out);
  and and_8 (and_8_out, or_3_out, xor_8_out);
  LED Carry_Out_0 (.in(or_1_out));
  or or_1 (or_1_out, and_5_out, and_1_out);
  LED Carry_Out_1 (.in(or_2_out));
  or or_2 (or_2_out, and_6_out, and_2_out);
  LED Carry_Out_2 (.in(or_3_out));
  or or_3 (or_3_out, and_7_out, and_3_out);
  or or_4 (or_4_out, and_8_out, and_4_out);
  LED Carry_Out_3 (.in(or_4_out));

  assign out_3[3:0] = out_3[7:4];
endmodule

module Comparador (
  input  [3:0] A,
  input  [3:0] B,
  output out_3
);

  wire A0_B0_2_out, A0_B0_out, A1_B1_2_out, A1_B1_out, A2_B2_2_out, A2_B2_out, A3_B3_2_out, A3_B3_out,
       A_B_2_out, A_B_out, E_2_out, E_3_out, E_out;

  and A3_B3 (A3_B3_out, ~A[3], B[3]);  // AND_Gate
  xnor A3_B3_2 (A3_B3_2_out, A[3], B[3]);
  and A2_B2 (A2_B2_out, ~A[2], B[2]);  // AND_Gate
  xnor A2_B2_2 (A2_B2_2_out, A[2], B[2]);
  and A1_B1 (A1_B1_out, ~A[1], B[1]);  // AND_Gate
  xnor A1_B1_2 (A1_B1_2_out, A[1], B[1]);
  and A0_B0 (A0_B0_out, ~A[0], B[0]);  // AND_Gate
  xnor A0_B0_2 (A0_B0_2_out, A[0], B[0]);
  and E (E_out, A3_B3_2_out, A2_B2_2_out, A1_B1_out);
  and E_2 (E_2_out, A3_B3_2_out, A2_B2_out);
  and E_3 (E_3_out, A3_B3_2_out, A2_B2_2_out, A1_B1_2_out, A0_B0_out);
  or A_B (A_B_out, A3_B3_out, E_2_out, E_out, E_3_out);
  and A_B_2 (A_B_2_out, A3_B3_2_out, A2_B2_2_out, A1_B1_2_out, A0_B0_2_out);
  // AND_Gate A_B_3 has open pins: in0=A_B_out, in4=A_B_2_out, out=open
  or A_B_ou_A_B (out_3, A_B_out, A_B_2_out);
endmodule

module Conversor_Gray (
  input  [3:0] A,
  input  [3:0] B,
  output [7:0] out_3
);

  wire multiplexer_1_out, multiplexer_2_out, multiplexer_3_out, multiplexer_4_out;

  Multiplexer #(.enable("false")) multiplexer_1 (.in0(A[2]), .in1(out_3[2]), .out(multiplexer_1_out), .sel(1'b0));
  Multiplexer #(.enable("false")) multiplexer_2 (.in0(A[1]), .in1(out_3[1]), .out(multiplexer_2_out), .sel(1'b0));
  xor xor_1 (out_3[2], A[3], A[2]);
  xor xor_2 (out_3[1], multiplexer_1_out, A[1]);
  xor xor_3 (out_3[0], multiplexer_2_out, A[0]);
  xor xor_4 (out_3[6], B[3], B[2]);
  Multiplexer #(.enable("false")) multiplexer_3 (.in0(B[2]), .in1(out_3[6]), .out(multiplexer_3_out), .sel(1'b0));
  Multiplexer #(.enable("false")) multiplexer_4 (.in0(B[1]), .in1(out_3[5]), .out(multiplexer_4_out), .sel(1'b0));
  xor xor_5 (out_3[5], multiplexer_3_out, B[1]);
  xor xor_6 (out_3[4], multiplexer_4_out, B[0]);

  assign {out_3[7], out_3[3]} = {B[3], A[3]};
endmodule

module _4___4___8 (
);
endmodule
